# Fritzing sketch Extruder (saved by Fritzing 0.9.7b)

parts:
  Part1 = Arduino Uno (Rev3)
  LCD1 = LCD screen
  Part2 = Adafruit I2C+SPI LCD Backpack [part_number="Adafruit #292"]
  SW1 = ENCODER_RGB_CA [package=encoder_led_3]  # not connected

nets:
  GND: Part1.GND, LCD1.VSS, LCD1.R/W, Part2.GND
  SDA: Part1.A4/SDA, Part2.DATA
  SCL: Part1.A5/SCL, Part2.CLOCK
  5V: Part1.5V, LCD1.VDD, LCD1.LED+, Part2.VCC
  N1: LCD1.V0, Part2.CONTRAST
  N2: LCD1.RS, Part2.RS
  N3: LCD1.E, Part2.E
  N4: LCD1.DB0, Part2.DB0
  N5: LCD1.DB1, Part2.DB1
  N6: LCD1.DB2, Part2.DB2
  N7: LCD1.DB3, Part2.DB3
  N8: LCD1.DB4, Part2.DB4
  N9: LCD1.DB5, Part2.DB5
  N10: LCD1.DB6, Part2.DB6
  N11: LCD1.DB7, Part2.DB7
  N12: LCD1.LED-, Part2.LEDK

notes:
  5V Arduino
  5V Motor
  12V Motor

custom parts:
  Adafruit I2C+SPI LCD Backpack: LCD backpacks reduce the number of pins needed to connect to an LCD. LCDs are a fun and easy way to have your microcontroller project talk back to you. Character LCDs are common, and easy to get, available in tons of colors and sizes. We've written tutorials on using character LCDs with an Arduino (or similar microcontroller) but find that the number of pins necessary to control the LCD can be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
