# Fritzing sketch Spooler Controller (saved by Fritzing 0.9.8b)

parts:
  Part1 = Arduino Uno (Rev3)  # not connected
  LCD1 = LCD screen
  Part2 = Adafruit I2C+SPI LCD Backpack [part_number="Adafruit #292"]
  Part4 = Adafruit Proto Screwshield Wingshield [part_number="Adafruit #196"]
  M3 = DC Motor
  M4 = DC Motor
  R5 = Resistor [tolerance=±5% power=0.25 resistance=10k package=THT]
  Q3 = Basic FET N-Channel [part_number=STP16NF06 package="TO220 [THT]"]
  Q4 = Basic FET N-Channel [part_number=NTE2984 package="TO220 [THT]"]
  D5 = Rectifier Diode [part_number=1N5819 package="300 mil [THT]"]
  D6 = Rectifier Diode [part_number=1N5819 package="300 mil [THT]"]
  D7 = Rectifier Diode [part_number=1N5819 package="300 mil [THT]"]
  D8 = Rectifier Diode [part_number=1N5819 package="300 mil [THT]"]
  J9 = Screw terminal - 2 pins [package=THT]
  J11 = Screw terminal - 2 pins [package=THT]
  R7 = Resistor [tolerance=±5% power=0.25 resistance=150 package=THT]
  R8 = Resistor [tolerance=±5% power=0.25 resistance=150 package=THT]
  R6 = Resistor [tolerance=±5% power=0.25 resistance=10k package=THT]

nets:
  GND: LCD1.VSS, LCD1.R/W, Part2.GND, Part4.GND, Part4.N$59, Part4.N$275, R5.Pin_0, Q3.source, Q4.source, R6.Pin_1
  5V: LCD1.VDD, LCD1.LED+, Part2.VCC, Part4.+5V, Part4.N$101, M4.pin_1, D6.cathode, J11.pin1
  N1: LCD1.V0, Part2.CONTRAST
  N2: LCD1.RS, Part2.RS
  N3: LCD1.E, Part2.E
  N4: LCD1.DB0, Part2.DB0
  N5: LCD1.DB1, Part2.DB1
  N6: LCD1.DB2, Part2.DB2
  N7: LCD1.DB3, Part2.DB3
  N8: LCD1.DB4, Part2.DB4
  N9: LCD1.DB5, Part2.DB5
  N10: LCD1.DB6, Part2.DB6
  N11: LCD1.DB7, Part2.DB7
  N12: LCD1.LED-, Part2.LEDK
  SCL: Part2.CLOCK, Part4.SCL
  SDA: Part2.DATA, Part4.SDA
  12V: Part4.VIN, M3.pin_1, D5.cathode, J9.pin2
  Signal2: Part4.A1, R5.Pin_1, R8.Pin_1
  Signal1: Part4.A0, Part4.N$92, Part4.N$266, R7.Pin_1, R6.Pin_0
  N13: Part4.N$52, Part4.N$55, Q4.gate, R7.Pin_0
  N14: Part4.N$56, Part4.N$60, Q4.drain, D8.cathode
  MOTOR 5V: Part4.N$68, Part4.N$73, Part4.N$102, M4.pin_2, D6.anode, D8.anode, J11.pin2
  MOTOR 12V: M3.pin_2, D5.anode, D7.anode, J9.pin1
  N15: Q3.gate, R8.Pin_0
  N16: Q3.drain, D7.cathode

notes:
  5V Arduino
  5V Motor
  12V Motor

custom parts:
  Adafruit I2C+SPI LCD Backpack: LCD backpacks reduce the number of pins needed to connect to an LCD. LCDs are a fun and easy way to have your microcontroller project talk back to you. Character LCDs are common, and easy to get, available in tons of colors and sizes. We've written tutorials on using character LCDs with an Arduino (or similar microcontroller) but find that the number of pins necessary to control the LCD can be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
  Adafruit Proto Screwshield Wingshield: The next generation Proto-ScrewShield is a dual-purpose prototyping shield. Not only does it have a large 0.1" grid prototyping area but it also extends the Arduino pins to sturdy, secure, and dependable screw terminal blocks. You even get a few bonus terminals for extra GND and four 'free' terminals for whatever connections you wish! New! As of June 23, 2014 we now have an R3 update to this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
