# Fritzing sketch Spooler Motor Adaptor (saved by Fritzing 0.9.6b)
breadboards: 1

parts:
  JACK1 = 2.1mm DC Barrel Jack
  M1 = DC Motor
  J1 = female pin header, 3 pins [form="♀ (female)"]
  J2 = female pin header, 3 pins [form="♀ (female)"]
  D1 = Rectifier Diode [part_number=1N4001 package="300 mil [THT]"]

nets:
  N1: JACK1.center, M1.pin_1, J1.pin3, J2.pin3, D1.cathode
  N2: JACK1.switch, JACK1.sleeve, M1.pin_2, J1.pin1, J1.pin2, J2.pin1, J2.pin2, D1.anode

custom parts:
  2.1mm DC Barrel Jack: 2.1mm DC Barrel Jack with Thru-Hole Connectors (breadboardable)
