# Fritzing sketch Spooler Motor Driver (saved by Fritzing 0.9.7b)
perfboards: 1

parts:
  Q1 = Basic FET N-Channel [part_number=NTE2984 package="TO220 [THT]"]
  D1 = Rectifier Diode [part_number=1N5819 package="300 mil [THT]"]
  D2 = Rectifier Diode [part_number=1N5819 package="300 mil [THT]"]
  J1 = Screw terminal - 2 pins [package=THT]
  J2 = Screw terminal - 2 pins [package=THT]
  J3 = Screw terminal - 2 pins [package=THT]
  R1 = Resistor [tolerance=±5% power=0.25 resistance=10k package=THT]
  J5 = Screw terminal - 2 pins [package=THT]
  J4 = Screw terminal - 2 pins [package=THT]
  Q2 = Basic FET N-Channel [part_number=STP16NF06 package="TO220 [THT]"]
  D3 = Rectifier Diode [part_number=1N5819 package="300 mil [THT]"]
  D4 = Rectifier Diode [part_number=1N5819 package="300 mil [THT]"]
  J6 = Screw terminal - 2 pins [package=THT]
  R4 = Resistor [tolerance=±5% power=0.25 resistance=150 package=THT]
  R3 = Resistor [tolerance=±5% power=0.25 resistance=10k package=THT]
  R2 = Resistor [tolerance=±5% power=0.25 resistance=150 package=THT]
  M1 = DC Motor
  M2 = DC Motor

nets:
  N1: Q1.gate, R2.Pin_0
  N2: Q1.drain, D2.cathode
  GND: Q1.source, J1.pin1, J3.pin2, R1.Pin_1, J4.pin2, Q2.source, J6.pin1, R3.Pin_0
  5V: D1.cathode, J1.pin2, J2.pin1, M1.pin_1
  MOTOR 5V: D1.anode, D2.anode, J2.pin2, M1.pin_2
  Signal1: J3.pin1, R1.Pin_0, R2.Pin_1
  MOTOR 12V: J5.pin1, D3.anode, D4.anode, M2.pin_2
  12V: J5.pin2, J4.pin1, D3.cathode, M2.pin_1
  N3: Q2.gate, R4.Pin_0
  N4: Q2.drain, D4.cathode
  Signal2: J6.pin2, R4.Pin_1, R3.Pin_1

notes:
  Left Terminals:
  Top: 5V, Gnd
  Mid: 5V Motor
  Low: Signal, Gnd
  Right Terminals:
  Top: 12V, Gnd
  Mid: 12V Motor
  Low: Signal, Gnd
  12V Power
  12V Motor
  5V Arduino
  5V Power
  5V Motor
